// Digital circuit circuit_counter.dig as structural Verilog
module circuit_counter (
  input  [7:0] In,
  input  [3:0] Rn,
  output Nlo,
  output NLb,
  output Eu,
  output Su_2,
  output Su_1,
  output Su_0,
  output NLa,
  output NCl,
  output NLi,
  output NCe,
  output LNm,
  output Ep,
  output Cp
);

  wire [12:0] Instructions_d;

  ROM #(.AddrBits(8), .Bits(13)) Instructions (.A(In), .sel(1'b1), .D(Instructions_d));
  assign {Cp, Ep, LNm, NCe, NLi, NCl, NLa, Su_0, Su_1, Su_2, Eu, NLb, Nlo} = Rn[3] ? Instructions_d : 13'bz;  // Driver driver_1
  assign {Cp, Ep, LNm, NCe, NLi, NCl, NLa, Su_0, Su_1, Su_2, Eu, NLb, Nlo} = Rn[2] ? 13'h4c3 : 13'bz;  // Driver driver_2
  assign {Cp, Ep, LNm, NCe, NLi, NCl, NLa, Su_0, Su_1, Su_2, Eu, NLb, Nlo} = Rn[1] ? 13'h17c3 : 13'bz;  // Driver driver_3
  assign {Cp, Ep, LNm, NCe, NLi, NCl, NLa, Su_0, Su_1, Su_2, Eu, NLb, Nlo} = Rn[0] ? 13'hbc3 : 13'bz;  // Driver driver_4

  // Notes on the sheet:
  //   contents of Instructions (hex, n*v repeats v):
  //   bc3,5c1,bc3,583,7c6,743
endmodule
