// Digital circuit cpu.dig as structural Verilog
module cpu (
  input  Clk,
  input  Rc
);

  wire Cp, Ep, Eu, Execute, Fetch, NCe, NCl, NLa, NLb, NLi, NLm, Nlo, not_1_out, or_1_out, plus____out, Su_0,
       Su_1, Su_2;
  wire [1:0] ring_counter_1_q;
  wire [3:0] Din_0, Din_1, R_0, R_1;
  wire [7:0] A_a, A_b, alu_1_s, B_in, counter_1_out, IR, IR_q, MAR_q, out;

  Counter #(.Bits(8)) counter_1 (.en(1'b1), .C(Cp), .clr(~NCl), .out(counter_1_out));  // open: ovf
  Register #(.Bits(8)) MAR (.D(B_in), .C(NLm), .en(1'b1), .Q(MAR_q));
  Register #(.Bits(8)) u_IR (.D(B_in), .C(Clk), .en(~NLi), .Q(IR_q));
  ring_counter ring_counter_1 (.Clk(Rc), .Q({Execute, Fetch, ring_counter_1_q}));
  // Probe on counter_1_out
  not not_1 (not_1_out, NCe);
  // Probe on out
  assign out = Ep ? counter_1_out : 8'bz;  // Driver driver_1
  // Probe on MAR_q
  ROM #(.AddrBits(8), .Bits(8)) rom_1 (.A(MAR_q), .sel(not_1_out), .D(out));
  assign IR = Execute ? IR_q : 8'bz;  // Driver driver_2
  circuit_counter circuit_counter_1 (
    .In(IR), .Rn({Execute, Fetch, ring_counter_1_q}), .Nlo(Nlo), .NLb(NLb), .Eu(Eu), .Su_2(Su_2),
    .Su_1(Su_1), .Su_0(Su_0), .NLa(NLa), .NCl(NCl), .NLi(NLi), .NCe(NCe), .LNm(NLm), .Ep(Ep), .Cp(Cp));
  // Probe on IR
  or or_1 (or_1_out, Ep, Eu, ~NCe);  // Or
  // Probe on out
  Register #(.Bits(8)) Bus_w (.D(out), .C(Clk), .en(or_1_out), .Q(B_in));
  // Probe on B_in
  // Probe on A_a
  // Probe on A_b
  // Probe on B_in
  Register #(.Bits(8)) AC (.D(B_in), .C(Clk), .en(~NLa), .Q(A_a));
  // Probe on Eu
  alu alu_1 (.A(A_a), .B(A_b), .OP({Su_2, Su_1, Su_0}), .S(alu_1_s), .R({R_1, R_0}), .plus(plus____out));
  // Probe on B_in
  Register #(.Bits(8)) B (.D(B_in), .C(Clk), .en(~NLb), .Q(A_b));
  // Probe on B_in
  Register #(.Bits(8)) u_out (.D(B_in), .C(Clk), .en(~Nlo), .Q({Din_1, Din_0}));
  // Probe on A_a
  // Probe on out
  assign out = Eu ? alu_1_s : 8'bz;  // Driver driver_3
  // Probe on A_b
  // Probe on Din_0
  // Probe on Din_1
  LED led_1 (.in(plus____out));
  Seven_Seg_Hex seven_seg_hex_1 (.d(Din_1), .dp(1'b0));
  Seven_Seg_Hex seven_seg_hex_2 (.d(R_1), .dp(1'b0));
  Seven_Seg_Hex seven_seg_hex_3 (.d(Din_0), .dp(1'b0));
  Seven_Seg_Hex seven_seg_hex_4 (.d(R_0), .dp(1'b0));

  // Notes on the sheet:
  //   Clk: Hz: 5
  //   contents of rom_1 (hex, n*v repeats v):
  //   0,1,2,3,4,5
endmodule
