// Digital circuit ir.dig as structural Verilog
module ir (
  input  [7:0] D_in,
  input  Clk,
  input  IR,
  output [7:0] out
);

  Register #(.Bits(8)) register_1 (.D(D_in), .C(Clk), .en(~IR), .Q(out));
endmodule
