// Digital circuit Registrador de Instrução (IR).dig as structural Verilog
module \Registrador_de_Instrução__IR  (
  input  [7:0] a,
  input  clk
);

  wire [7:0] IR_q;

  Register #(.Bits(8)) IR (.D(a), .C(clk), .Q(IR_q));  // open: en
endmodule
