// Digital circuit alu.dig as structural Verilog
module alu (
  input  [7:0] A,
  input  [7:0] B,
  input  [2:0] OP,
  output [7:0] S,
  output [7:0] R,
  output plus
);

  wire n;
  wire [3:0] divisor_4bits_1_r, divisor_4bits_1_s;
  wire [7:0] out_dec, out_div, out_inc, out_mult, out_sub, out_sum, resto;

  somador_8bits somador_8bits_1 (.A(A), .B(B), .out(out_sum));  // open: Co
  subtrator_completo subtrator_completo_1 (.A(A), .B(B), .S(out_sub), .out_4(n));
  multiplicador multiplicador_1 (.A(A[3:0]), .B(B[3:0]), .S(out_mult));
  divisor_4bits divisor_4bits_1 (.D(A[3:0]), .d_2(B[3:0]), .S(divisor_4bits_1_s), .r(divisor_4bits_1_r));
  inc inc_1 (.A(A), .S(out_inc));
  dec dec_1 (.A(A), .S(out_dec));
  BitExtender #(.inputBits(4), .outputBits(8)) bitextender_1 (.in(divisor_4bits_1_s), .out(out_div));
  BitExtender #(.inputBits(4), .outputBits(8)) bitextender_2 (.in(divisor_4bits_1_r), .out(resto));
  Multiplexer #(.Bits(8), .Selector_Bits(3)) multiplexer_1 (
    .sel(OP), .in_0({8{1'b0}}), .in_1({8{1'b0}}), .in_2({8{1'b0}}), .in_3(resto), .in_4({8{1'b0}}),
    .in_5({8{1'b0}}), .in_6({8{1'b0}}), .in_7({8{1'b0}}), .out(R));
  Multiplexer #(.Selector_Bits(3), .Bits(8)) multiplexer_2 (
    .sel(OP), .in_0(out_sum), .in_1(out_sub), .in_2(out_mult), .in_3(out_div), .in_4(out_inc),
    .in_5(out_dec), .in_6({8{1'b0}}), .in_7({8{1'b0}}), .out(S));
  Multiplexer #(.Selector_Bits(3)) multiplexer_3 (
    .sel(OP), .in_0(1'b0), .in_1(n), .in_2(1'b0), .in_3(1'b0), .in_4(1'b0), .in_5(1'b0), .in_6(1'b0),
    .in_7(1'b0), .out(plus));

  // Other names for the same wires on the sheet: A_4[3:0] = A[3:0]; B_4[3:0] = B[3:0]; Selecao_op[2:0] = OP
endmodule
