// Digital circuit multiplicador.dig as structural Verilog
module multiplicador (
  input  [3:0] A,
  input  [3:0] B,
  output [7:0] S
);

  wire [3:0] and_1_out;
  wire [4:1] and_5_out;
  wire [5:2] and_9_out;
  wire [6:3] and_13_out;
  wire [7:0] somador_8bits_1_out, somador_8bits_2_out;

  and and_1 (and_1_out[0], A[0], B[0]);
  and and_2 (and_1_out[1], A[0], B[1]);
  and and_3 (and_1_out[2], A[0], B[2]);
  and and_4 (and_1_out[3], A[0], B[3]);
  and and_5 (and_5_out[1], A[1], B[0]);
  and and_6 (and_5_out[2], A[1], B[1]);
  and and_7 (and_5_out[3], A[1], B[2]);
  and and_8 (and_5_out[4], A[1], B[3]);
  and and_9 (and_9_out[2], A[2], B[0]);
  and and_10 (and_9_out[3], A[2], B[1]);
  and and_11 (and_9_out[4], A[2], B[2]);
  and and_12 (and_9_out[5], A[2], B[3]);
  and and_13 (and_13_out[3], A[3], B[0]);
  and and_14 (and_13_out[4], A[3], B[1]);
  and and_15 (and_13_out[5], A[3], B[2]);
  and and_16 (and_13_out[6], A[3], B[3]);
  somador_8bits somador_8bits_1 (
    .A({4'b0000, and_1_out}), .B({3'b000, and_5_out, 1'b0}), .out(somador_8bits_1_out));  // open: Co
  somador_8bits somador_8bits_2 (
    .A(somador_8bits_1_out), .B({2'b00, and_9_out, 2'b00}), .out(somador_8bits_2_out));  // open: Co
  somador_8bits somador_8bits_3 (.A(somador_8bits_2_out), .B({1'b0, and_13_out, 3'b000}), .out(S));  // open: Co
endmodule
