// Digital circuit somador-4bits.dig as structural Verilog
module somador_4bits (
  input  [3:0] A,
  input  [3:0] B,
  output Co,
  output [3:0] out
);

  wire somador_full_add_s6_1_co, somador_full_add_s6_2_co, somador_full_add_s6_3_co;

  somador_full_add_s6 somador_full_add_s6_1 (.A(A[0]), .B(B[0]), .Ci(1'b0), .S(out[0]), .Co(somador_full_add_s6_1_co));
  somador_full_add_s6 somador_full_add_s6_2 (
    .A(A[1]), .B(B[1]), .Ci(somador_full_add_s6_1_co), .S(out[1]), .Co(somador_full_add_s6_2_co));
  somador_full_add_s6 somador_full_add_s6_3 (
    .A(A[2]), .B(B[2]), .Ci(somador_full_add_s6_2_co), .S(out[2]), .Co(somador_full_add_s6_3_co));
  somador_full_add_s6 somador_full_add_s6_4 (.A(A[3]), .B(B[3]), .Ci(somador_full_add_s6_3_co), .S(out[3]), .Co(Co));
endmodule
