// Digital circuit somador-8bits.dig as structural Verilog
module somador_8bits (
  input  [7:0] A,
  input  [7:0] B,
  output [7:0] out,
  output Co
);

  wire somador_full_add_s6_1_co, somador_full_add_s6_2_co, somador_full_add_s6_3_co,
       somador_full_add_s6_4_co, somador_full_add_s6_5_co, somador_full_add_s6_6_co, somador_full_add_s6_7_co;

  somador_full_add_s6 somador_full_add_s6_1 (.A(A[0]), .B(B[0]), .Ci(1'b0), .S(out[0]), .Co(somador_full_add_s6_1_co));
  somador_full_add_s6 somador_full_add_s6_2 (
    .A(A[1]), .B(B[1]), .Ci(somador_full_add_s6_1_co), .S(out[1]), .Co(somador_full_add_s6_2_co));
  somador_full_add_s6 somador_full_add_s6_3 (
    .A(A[2]), .B(B[2]), .Ci(somador_full_add_s6_2_co), .S(out[2]), .Co(somador_full_add_s6_3_co));
  somador_full_add_s6 somador_full_add_s6_4 (
    .A(A[3]), .B(B[3]), .Ci(somador_full_add_s6_3_co), .S(out[3]), .Co(somador_full_add_s6_4_co));
  somador_full_add_s6 somador_full_add_s6_5 (
    .A(A[4]), .B(B[4]), .Ci(somador_full_add_s6_4_co), .S(out[4]), .Co(somador_full_add_s6_5_co));
  somador_full_add_s6 somador_full_add_s6_6 (
    .A(A[5]), .B(B[5]), .Ci(somador_full_add_s6_5_co), .S(out[5]), .Co(somador_full_add_s6_6_co));
  somador_full_add_s6 somador_full_add_s6_7 (
    .A(A[6]), .B(B[6]), .Ci(somador_full_add_s6_6_co), .S(out[6]), .Co(somador_full_add_s6_7_co));
  somador_full_add_s6 somador_full_add_s6_8 (.A(A[7]), .B(B[7]), .Ci(somador_full_add_s6_7_co), .S(out[7]), .Co(Co));
endmodule
