// Digital circuit somador-full-add-s6.dig as structural Verilog
module somador_full_add_s6 (
  input  A,
  input  B,
  input  Ci,
  output S,
  output Co
);

  wire and_1_out, and_2_out, and_3_out;

  and and_1 (and_1_out, A, B);
  and and_2 (and_2_out, A, Ci);
  and and_3 (and_3_out, B, Ci);
  xor xor_1 (S, A, B, Ci);
  or or_1 (Co, and_1_out, and_2_out, and_3_out);
endmodule
