// Digital circuit subtrator-basic.dig as structural Verilog
module subtrator_basic (
  input  [7:0] A,
  input  [7:0] B,
  output Co,
  output [7:0] substract
);

  wire [7:0] not_1_out, somador_8bits_1_out;

  assign not_1_out = ~B;  // Not not_1, 8 bits wide
  somador_8bits somador_8bits_1 (.A(not_1_out), .B(8'h1), .out(somador_8bits_1_out));  // open: Co
  somador_8bits somador_8bits_2 (.A(A), .B(somador_8bits_1_out), .out(substract), .Co(Co));
endmodule
