// Digital circuit subtrator-completo.dig as structural Verilog
module subtrator_completo (
  input  [7:0] A,
  input  [7:0] B,
  output [7:0] S,
  output out_4
);

  wire [6:0] subtrator_basic_1_substract;
  wire [7:0] not_1_out, somador_8bits_1_out;

  subtrator_basic subtrator_basic_1 (.A(A), .B(B), .substract({out_4, subtrator_basic_1_substract}));  // open: Co
  assign not_1_out = ~{out_4, subtrator_basic_1_substract};  // Not not_1, 8 bits wide
  somador_8bits somador_8bits_1 (.A(not_1_out), .B(8'h1), .out(somador_8bits_1_out));  // open: Co
  assign S = out_4 ? somador_8bits_1_out : 8'bz;  // Driver driver_1
  assign S = ~out_4 ? {out_4, subtrator_basic_1_substract} : 8'bz;  // DriverInvSel driverinvsel_1
endmodule
