// Digital circuit program_counter.dig as structural Verilog
module program_counter (
  input  Cp,
  input  Reset,
  input  Ep,
  output [7:0] out
);

  wire [7:0] counter_1_out;

  Counter #(.Bits(8)) counter_1 (.en(1'b1), .C(Cp), .clr(Reset), .out(counter_1_out));  // open: ovf
  assign out = Ep ? counter_1_out : 8'bz;  // Driver driver_1

  // Other names for the same wires on the sheet: Clr = Reset
endmodule
