// Digital circuit unidade_de_controle.dig as structural Verilog
module unidade_de_controle (
  input  [7:0] INSTR,
  input  Clk_UC,
  output IR_load,
  output PC_en,
  output PC_ld,
  output ACC_load
);

  wire decoder_1_out_1, decoder_1_out_2, decoder_1_out_3, decoder_1_out_4, or_1_out, out_8, Q;

  Decoder #(.Selector_Bits(4)) decoder_1 (
    .sel(INSTR[3:0]), .out_1(decoder_1_out_1), .out_2(decoder_1_out_2), .out_3(decoder_1_out_3),
    .out_4(decoder_1_out_4), .out_8(out_8));  // open: out_0, out_5, out_6, out_7, out_9, out_10, out_11, out_12, out_13, out_14, out_15
  or or_1 (or_1_out, decoder_1_out_1, decoder_1_out_2, decoder_1_out_3, decoder_1_out_4);
  and and_1 (ACC_load, or_1_out, Q);
  T_FF Ciclo_Fetch_Exec (.T(1'b1), .C(Clk_UC), .Q(IR_load), .nQ(Q));
  and and_2 (PC_ld, Q, out_8);

  assign PC_en = IR_load;
endmodule
